# Fritzing sketch Untitled Sketch (saved by Fritzing 0.9.3b)
breadboards: 2

parts:
  Led_Matrix_8x8 = LBT2088AH [part_number=LBT2088AH]
  Arduino_Mega = Arduino Mega 2560 (Rev3)

nets:
  N1: Led_Matrix_8x8.pin1, Arduino_Mega.D47
  N2: Led_Matrix_8x8.pin2, Arduino_Mega.D51
  N3: Led_Matrix_8x8.pin_3, Arduino_Mega.D40
  N4: Led_Matrix_8x8.pin_4, Arduino_Mega.D42
  N5: Led_Matrix_8x8.pin_5, Arduino_Mega.D53
  N6: Led_Matrix_8x8.pin_6, Arduino_Mega.D46
  N7: Led_Matrix_8x8.pin_7, Arduino_Mega.D49
  N8: Led_Matrix_8x8.pin_8, Arduino_Mega.D43
  N9: Led_Matrix_8x8.pin_9, Arduino_Mega.D39
  N10: Led_Matrix_8x8.pin_10, Arduino_Mega.D44
  N11: Led_Matrix_8x8.pin_11, Arduino_Mega.D48
  N12: Led_Matrix_8x8.pin_12, Arduino_Mega.D45
  N13: Led_Matrix_8x8.pin_13, Arduino_Mega.D38
  N14: Led_Matrix_8x8.pin_14, Arduino_Mega.D41
  N15: Led_Matrix_8x8.pin_15, Arduino_Mega.D50
  N16: Led_Matrix_8x8.pin_16, Arduino_Mega.D52
