# Fritzing sketch semaforo (saved by Fritzing 0.9.3b)
circuit board: 8.46667cm x 5.64444cm
breadboards: 1

parts:
  Part1 = Arduino Mega 2560 (Rev3)
  S1 = Pushbutton [package="[THT]"]
  LED1 = LED - 5mm [color="Blue (505nm)" package="5 mm [THT]"]
  R1 = Resistor [tolerance=±5% resistance=220 package=THT]
  LED2 = LED - 5mm [color="Red (633nm)" package="5 mm [THT]"]
  LED3 = LED - 5mm [color="Red (633nm)" package="5 mm [THT]"]
  LED4 = LED - 5mm [color="Yellow (595nm)" package="5 mm [THT]"]
  LED5 = LED - 5mm [color="Yellow (595nm)" package="5 mm [THT]"]
  LED6 = LED - 5mm [color="Green (555nm)" package="5 mm [THT]"]
  LED7 = LED - 5mm [color="Green (555nm)" package="5 mm [THT]"]
  R2 = Resistor [tolerance=±5% resistance=220 package=THT]
  R3 = Resistor [tolerance=±5% resistance=220 package=THT]
  R4 = Resistor [tolerance=±5% resistance=220 package=THT]
  R5 = Resistor [tolerance=±5% resistance=220 package=THT]
  R6 = Resistor [tolerance=±5% resistance=220 package=THT]
  R7 = Resistor [tolerance=±5% resistance=220 package=THT]
  R8 = Resistor [tolerance=±5% resistance=220 package=THT]

nets:
  N1: Part1.GND, R1.Pin_0, R2.Pin_0, R3.Pin_0, R4.Pin_0, R5.Pin_0, R6.Pin_0, R7.Pin_0, R8.Pin_1
  N2: Part1.D13_PWM, LED1.anode
  N3: Part1.D12_PWM, LED2.anode
  N4: Part1.D11_PWM, LED4.anode
  N5: Part1.D10_PWM, LED6.anode
  N6: Part1.5V, S1.Pin_1, S1.Pin_2
  N7: Part1.D2_PWM, S1.Pin_3, S1.Pin_4, R8.Pin_0
  N8: Part1.D5_PWM, LED7.anode
  N9: Part1.D6_PWM, LED5.anode
  N10: Part1.D7_PWM, LED3.anode
  N11: LED1.cathode, R1.Pin_1
  N12: LED2.cathode, R2.Pin_1
  N13: LED3.cathode, R5.Pin_1
  N14: LED4.cathode, R3.Pin_1
  N15: LED5.cathode, R6.Pin_1
  N16: LED6.cathode, R4.Pin_1
  N17: LED7.cathode, R7.Pin_1
