# Fritzing sketch upAndDownLed (saved by Fritzing 0.9.3b)
breadboards: 1

parts:
  LED7 = LED - 5mm [color="Red (633nm)" package="5 mm [THT]"]
  LED8 = LED - 5mm [color="Red (633nm)" package="5 mm [THT]"]
  LED9 = LED - 5mm [color="Red (633nm)" package="5 mm [THT]"]
  R15 = Resistor [tolerance=±5% resistance=220 package=THT]
  R16 = Resistor [tolerance=±5% resistance=220 package=THT]
  R17 = Resistor [tolerance=±5% resistance=220 package=THT]
  R18 = Resistor [tolerance=±5% resistance=220 package=THT]
  R19 = Resistor [tolerance=±5% resistance=220 package=THT]
  R20 = Resistor [tolerance=±5% resistance=220 package=THT]
  S5 = Pushbutton [package="[THT]"]
  S6 = Pushbutton [package="[THT]"]
  R21 = Rotary Potentiometer (Small) [maximum_resistance=100kΩ package=THT]
  Part4 = Arduino Mega 2560 (Rev3)

nets:
  N1: LED7.cathode, R17.Pin_1
  N2: LED7.anode, Part4.D11_PWM
  N3: LED8.cathode, R19.Pin_1
  N4: LED8.anode, Part4.D13_PWM
  N5: LED9.cathode, R16.Pin_1
  N6: LED9.anode, Part4.D12_PWM
  N7: R15.Pin_0, S6.Pin_3, S6.Pin_4, Part4.D2_PWM
  N8: R15.Pin_1, R16.Pin_0, R17.Pin_0, R19.Pin_0, S5.Pin_1, S5.Pin_2, R21.leg2, Part4.GND
  N9: R18.Pin_0, S5.Pin_3, S5.Pin_4, Part4.D3_PWM
  N10: R18.Pin_1, R20.Pin_1, S6.Pin_1, S6.Pin_2, Part4.5V
  N11: R20.Pin_0, R21.leg1
  N12: R21.wiper, Part4.A0

// code stored in the sketch: upAndDownLed.ino
/*
 * Author: Giulio Bosco (giulio.bosco@samtrevano.ch)
 */

int upButton = 3;               // Button in pull-up pin
int downButton = 2;             // Button in pull-down pin

int potentiometer = 0;          // Potentiometer pin

int upLed = 13;                 // Led for pull-up button pin
int downLed = 12;               // Led for pull-down button pin
int potentiometerLed = 11;      // Potentiometer pin


void setup() {
  // put your setup code here, to run once:
  pinMode(upButton, INPUT);     // setup upButton pin to use as input
  pinMode(downButton, INPUT);   // setup downButton pin to use ase input

  pinMode(upLed, OUTPUT);       // setup upLed pin to use as output
  pinMode(downLed, OUTPUT);     // setup downLed pin to use as output
  pinMode(potentiometerLed, OUTPUT); // setup potentiometerLed to use as output
}

void loop() {
  // put your main code here, to run repeatedly:
  if (digitalRead(upButton)) {
    digitalWrite(upLed,HIGH);
  } else {
    digitalWrite(upLed,LOW);
  }

  if (digitalRead(downButton)) {
    digitalWrite(downLed,HIGH);
  } else {
    digitalWrite(downLed,LOW);
  }

  int potentiometerIN = analogRead(potentiometer);
  analogWrite(potentiometerLed, potentiometerIN);
}
